# Fritzing sketch bme280 digispark (saved by Fritzing 0.9.2b)

parts:
  Digispark1 = Digispark
  Bauteil1 = Adafruit BME280

nets:
  VCC: Digispark1.VCC, Bauteil1.VIN
  GND: Digispark1.GND, Bauteil1.GND
  N1: Digispark1.P0, Bauteil1.SDI/SDA
  N2: Digispark1.P2, Bauteil1.SCK/SCL

custom parts:
  Digispark: The Digispark is an Attiny85 based microcontroller development board similar to the Arduino line, only cheaper, smaller, and a bit less powerful. With a whole host of shields to extend its functionality and the ability to use the familiar Arduino IDE the Digispark is a great way to jump into electronics, or perfect for when an Arduino is too big or too much.
  Adafruit BME280: Bosch has stepped up their game with their new BME280 sensor, an environmental sensor with temperature, barometric pressure and humidity! This sensor is great for all sorts of weather/environmental sensing and can even be used in both I2C and SPI! This precision sensor from Bosch is the best low-cost sensing solution for measuring humidity with ±3% accuracy, barometric pressure with ±1 hPa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
