# Fritzing sketch bme280 nodemcu (saved by Fritzing 0.9.2b)

parts:
  U1 = NodeMCU V1.0
  Bauteil1 = Adafruit BME280
  R1 = Resistor [tolerance=±5% resistance=3.3k package=THT]

nets:
  GND: U1.D1, U1.GND, U1.D5, U1.D6, U1.D7, U1.D8, Bauteil1.GND, Bauteil1.SCK/SCL, Bauteil1.SDO/ADR, Bauteil1.SDI/SDA, Bauteil1.CS, R1.Pin_0, R1.Pin_1
  3V3: U1.3V3, Bauteil1.VIN

custom parts:
  NodeMCU V1.0: ESP8266 based NodeMCU V1.0
  Adafruit BME280: Bosch has stepped up their game with their new BME280 sensor, an environmental sensor with temperature, barometric pressure and humidity! This sensor is great for all sorts of weather/environmental sensing and can even be used in both I2C and SPI! This precision sensor from Bosch is the best low-cost sensing solution for measuring humidity with ±3% accuracy, barometric pressure with ±1 hPa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
