# Fritzing sketch photoresistor digispark (saved by Fritzing 0.9.2b)

parts:
  Digispark1 = Digispark
  R1 = Resistor [tolerance=±5% resistance=220 package=THT]
  R2 = Photocell (LDR) [package=THT]

nets:
  N1: Digispark1.VCC, R2.pin_1
  N2: Digispark1.GND, R1.Pin_1
  N3: Digispark1.P2, R1.Pin_0, R2.pin_0

custom parts:
  Digispark: The Digispark is an Attiny85 based microcontroller development board similar to the Arduino line, only cheaper, smaller, and a bit less powerful. With a whole host of shields to extend its functionality and the ability to use the familiar Arduino IDE the Digispark is a great way to jump into electronics, or perfect for when an Arduino is too big or too much.
