# Fritzing sketch photoresistor nodemcu (saved by Fritzing 0.9.2b)

parts:
  U1 = NodeMCU V1.0
  R1 = Resistor [tolerance=±5% resistance=220 package=THT]
  R2 = Photocell (LDR) [package=THT]

nets:
  N1: U1.3V3, R2.pin_0
  N2: U1.GND, R1.Pin_0
  N3: U1.A0, R1.Pin_1, R2.pin_1

custom parts:
  NodeMCU V1.0: ESP8266 based NodeMCU V1.0
